// Logisim project final.circ as structural Verilog: 9 circuits, main circuit main
module main (
  input  [11:0] in_1,
  output [11:0] out_2
);

  wire branch_1_branch, clk, control_1_nop, not_2_out, or_1_out, regW_WB;
  wire [1:0] ex_mem_1_out_10, forwarding_1_r1, forwarding_1_r2, id_ex_1_out_15, id_ex_1_out_16,
       mem_wb_1_out_8, multiplexer_6_out;
  wire [2:0] ex_mem_1_out_9, id_ex_1_out_14_2;
  wire [7:0] control_1__0__aluin_reg2, id_ex_1_out_14, multiplexer_5_out;
  wire [11:0] adder_1_out, alu1, alu2, ex_mem_1_out_8, id_ex_1_out_10, id_ex_1_out_11, id_ex_1_out_12,
       id_ex_1_out_13, if_id_1_out_6, mem_wb_1_out_6, multiplexer_1_out, multiplexer_2_out,
       multiplexer_3_out, multiplexer_4_out, multiplexer_7_out, multiplexer_8_out, multiplexer_9_out,
       not_1_out, ram_1_data, ram_2_data, regfile_1_out_7, regfile_1_out_8, regfile_1_out_9,
       regfile_1_out_10, regfile_1_out_11, regfile_1_out_12, register_1_q, tun, tun2;

  Multiplexer #(.width(12), .enable("false")) multiplexer_1 (
    .in0(adder_1_out), .in1(tun2), .out(multiplexer_1_out), .sel(branch_1_branch));
  Clock clock_1 (.out(clk));
  Register #(.width(12)) register_1 (.D(multiplexer_1_out), .Q(register_1_q), .clk(clk));  // open: en, clr
  Register #(.width(12)) register_2 (.Q(out_2));  // open: D, en, clk, clr
  Adder #(.width(12)) adder_1 (.a(12'h1), .b(register_1_q), .out(adder_1_out));  // open: cin, cout
  RAM #(.addrWidth(12), .dataWidth(12), .bus("separate")) ram_1 (
    .addr(register_1_q), .data(ram_1_data));  // open: din, str, sel, clk, ld, clr
  Multiplexer #(.width(12)) multiplexer_2 (
    .in0(ram_1_data), .in1(12'h1), .out(multiplexer_2_out), .sel(branch_1_branch));  // open: en
  // Probe on in_1
  IF_ID if_id_1 (
    .in_1(register_1_q), .out_5(tun), .in_2(multiplexer_2_out), .out_6(if_id_1_out_6), .enable(1'b1),
    .clock(clk));
  // Probe on regfile_1_out_8
  // Probe on regfile_1_out_7
  RegFile regfile_1 (
    .m1_sel(if_id_1_out_6[8:7]), .in_2(mem_wb_1_out_6), .dec_sel(mem_wb_1_out_8),
    .m2_sel(if_id_1_out_6[6:5]), .write_enable(regW_WB), .out_7(regfile_1_out_7), .out_8(regfile_1_out_8),
    .out_9(regfile_1_out_9), .out_10(regfile_1_out_10), .out_11(regfile_1_out_11), .out_12(regfile_1_out_12),
    .clock(clk));
  Control control_1 (
    .op_code(if_id_1_out_6[11:9]), ._0__rd_3_4(control_1__0__aluin_reg2[7]),
    .Subtraction(control_1__0__aluin_reg2[1]), .beq(control_1__0__aluin_reg2[2]),
    .bne(control_1__0__aluin_reg2[3]), .load(control_1__0__aluin_reg2[5]),
    .reg_write(control_1__0__aluin_reg2[6]), .store(control_1__0__aluin_reg2[4]),
    ._0__ALUin_reg2(control_1__0__aluin_reg2[0]), .in_2(if_id_1_out_6[0]), .NOP(control_1_nop));
  Forwarding forwarding_1 (
    .readreg1(if_id_1_out_6[8:7]), .readreg2(if_id_1_out_6[6:5]), .writereg1(multiplexer_6_out),
    .writereg2(ex_mem_1_out_10), .r1(forwarding_1_r1), .r2(forwarding_1_r2));
  // Probe on regfile_1_out_10
  // Probe on regfile_1_out_9
  Multiplexer #(.select(2), .width(12)) multiplexer_3 (
    .in0(regfile_1_out_11), .in1(alu1), .in2(alu2), .out(multiplexer_3_out), .sel(forwarding_1_r1));  // open: in3, en
  Multiplexer #(.select(2), .width(12)) multiplexer_4 (
    .in0(regfile_1_out_12), .in1(alu1), .in2(alu2), .out(multiplexer_4_out), .sel(forwarding_1_r2));  // open: in3, en
  Multiplexer #(.width(8)) multiplexer_5 (
    .in0(control_1__0__aluin_reg2), .in1({8{1'b0}}), .out(multiplexer_5_out), .sel(or_1_out));  // open: en
  or or_1 (or_1_out, control_1_nop, branch_1_branch);
  ID_EX id_ex_1 (
    .in_1(tun), .in_2(multiplexer_3_out), .in_5(multiplexer_5_out), .in_6(if_id_1_out_6[4:3]), .in_8(1'b1),
    .in_9(clk), .out_10(id_ex_1_out_10), .out_11(id_ex_1_out_11),
    .out_14({id_ex_1_out_14[7], id_ex_1_out_14_2, id_ex_1_out_14[3:0]}), .out_15(id_ex_1_out_15),
    .in_7(if_id_1_out_6[6:5]), .out_16(id_ex_1_out_16), .in_3(multiplexer_4_out), .out_12(id_ex_1_out_12),
    .in_4({{7{1'b0}}, if_id_1_out_6[4:0]}), .out_13(id_ex_1_out_13));
  Multiplexer #(.width(2), .enable("false")) multiplexer_6 (
    .in0(id_ex_1_out_15), .in1(id_ex_1_out_16), .out(multiplexer_6_out), .sel(id_ex_1_out_14[7]));
  Adder #(.width(12)) adder_2 (.a(id_ex_1_out_10), .b(id_ex_1_out_13), .out(tun2));  // open: cin, cout
  Multiplexer #(.width(12), .enable("false")) multiplexer_7 (
    .in0(id_ex_1_out_12), .in1(id_ex_1_out_13), .out(multiplexer_7_out), .sel(id_ex_1_out_14[0]));
  assign not_1_out = ~multiplexer_7_out;  // NOT_Gate not_1, 12 bits wide
  Multiplexer #(.width(12), .enable("false")) multiplexer_8 (
    .in0(multiplexer_7_out), .in1(not_1_out), .out(multiplexer_8_out), .sel(id_ex_1_out_14[1]));
  Adder #(.width(12)) adder_3 (
    .a(id_ex_1_out_11), .b(multiplexer_8_out), .out(alu1), .cin(id_ex_1_out_14[1]));  // open: cout
  branch branch_1 (.in_1(alu1), .beq(id_ex_1_out_14[2]), .bne(id_ex_1_out_14[3]), .branch(branch_1_branch));
  EX_MEM ex_mem_1 (
    .in_1(alu1), .in_2(id_ex_1_out_12), .in_3(id_ex_1_out_14_2), .in_4(multiplexer_6_out), .in_5(1'b1),
    .in_6(clk), .out_7(alu2), .out_8(ex_mem_1_out_8), .out_9(ex_mem_1_out_9), .out_10(ex_mem_1_out_10));
  RAM #(.addrWidth(12), .dataWidth(12), .bus("separate")) ram_2 (
    .addr(alu2), .din(ex_mem_1_out_8), .data(ram_2_data), .str(ex_mem_1_out_9[0]), .clk(clk),
    .ld(ex_mem_1_out_9[1]));  // open: sel, clr
  not not_2 (not_2_out, ex_mem_1_out_9[1]);
  MEM_WB mem_wb_1 (
    .in_1(multiplexer_9_out), .in_2(ex_mem_1_out_9[2]), .in_3(ex_mem_1_out_10), .in_4(1'b1), .in_5(clk),
    .out_6(mem_wb_1_out_6), .out_7(regW_WB), .out_8(mem_wb_1_out_8));
  Multiplexer #(.width(12), .enable("false")) multiplexer_9 (
    .in0(ram_2_data), .in1(alu2), .out(multiplexer_9_out), .sel(not_2_out));
  // Probe on nothing

  // Notes on the sheet:
  //   Wired through tunnels to all clock inputs
  //   PC
  //   Instruction Memory
  //   branch hazard 2nd op after
  //   instruction binary to hex
  //   purely to help you convert
  //   and hex to binary!
  //   IF/ID
  //   r2
  //   r1
  //   r0
  //   Includes Branch forwarding Extra Credit above
  //   r3
  //   branch hazard 1st op after
  //   is NOP
  //   ID/EX
  //   EX/MEM
  //   Main Memory
  //   MEM/WB
endmodule

module Control (
  input  [2:0] op_code,
  input  in_2,
  output _0__ALUin_reg2,
  output Subtraction,
  output beq,
  output bne,
  output store,
  output load,
  output reg_write,
  output _0__rd_3_4,
  output NOP
);

  wire and_1_out, and_2_out, and_7_out, not_1_out, not_2_out, not_3_out;

  not not_1 (not_1_out, op_code[2]);
  not not_2 (not_2_out, op_code[1]);
  not not_3 (not_3_out, op_code[0]);
  and and_1 (and_1_out, op_code[2], not_2_out);
  or or_1 (Subtraction, and_1_out, and_2_out);
  and and_2 (and_2_out, op_code[0], not_1_out);
  and and_3 (beq, not_3_out, not_2_out, op_code[2]);
  and and_4 (bne, op_code[0], not_2_out, op_code[2]);
  and and_5 (store, not_3_out, op_code[1], op_code[2]);
  and and_6 (load, op_code[0], op_code[1], op_code[2]);
  and and_7 (and_7_out, op_code[0], op_code[1]);
  or or_2 (reg_write, and_7_out, not_1_out);
  or or_3 (_0__rd_3_4, op_code[2], op_code[1]);
  and and_8 (NOP, not_3_out, not_2_out, not_1_out, in_2);

  assign _0__ALUin_reg2 = op_code[1];

  // Notes on the sheet:
  //   op2 ~op2
  //   op1 ~op1
  //   op0 ~op0
  //   1: ALUin=imm 
  //   1: rd=5/6 
endmodule

module branch (
  input  [11:0] in_1,
  input  beq,
  input  bne,
  output branch
);

  wire and_1_out, and_2_out, not_1_out, or_1_out;

  or or_1 (or_1_out, in_1[0], in_1[1], in_1[2], in_1[3], in_1[4], in_1[5], in_1[6], in_1[7], in_1[8], in_1[9], in_1[10], in_1[11]);
  not not_1 (not_1_out, or_1_out);
  and and_1 (and_1_out, not_1_out, beq);
  and and_2 (and_2_out, or_1_out, bne);
  or or_2 (branch, and_1_out, and_2_out);

  // Notes on the sheet:
  //   ALU result
  //   if 0, r1==r2
  //   r1==r2
  //   r1!=r2
endmodule

module IF_ID (
  input  [11:0] in_1,
  input  [11:0] in_2,
  input  enable,
  input  clock,
  output [11:0] out_5,
  output [11:0] out_6
);

  Register #(.width(12)) register_1 (.D(in_1), .en(enable), .Q(out_5), .clk(clock));  // open: clr
  Register #(.width(12)) register_2 (.D(in_2), .en(enable), .Q(out_6), .clk(clock));  // open: clr
endmodule

module ID_EX (
  input  [11:0] in_1,
  input  [11:0] in_2,
  input  [11:0] in_3,
  input  [11:0] in_4,
  input  [7:0] in_5,
  input  [1:0] in_6,
  input  [1:0] in_7,
  input  in_8,
  input  in_9,
  output [11:0] out_10,
  output [11:0] out_11,
  output [11:0] out_12,
  output [11:0] out_13,
  output [7:0] out_14,
  output [1:0] out_15,
  output [1:0] out_16
);

  Register #(.width(12)) register_1 (.D(in_1), .en(in_8), .Q(out_10), .clk(in_9));  // open: clr
  Register #(.width(12)) register_2 (.D(in_2), .en(in_8), .Q(out_11), .clk(in_9));  // open: clr
  Register #(.width(12)) register_3 (.D(in_3), .en(in_8), .Q(out_12), .clk(in_9));  // open: clr
  Register #(.width(12)) register_4 (.D(in_4), .en(in_8), .Q(out_13), .clk(in_9));  // open: clr
  Register register_5 (.D(in_5), .en(in_8), .Q(out_14), .clk(in_9));  // open: clr
  Register #(.width(2)) register_6 (.D(in_6), .en(in_8), .Q(out_15), .clk(in_9));  // open: clr
  Register #(.width(2)) register_7 (.D(in_7), .en(in_8), .Q(out_16), .clk(in_9));  // open: clr
endmodule

module EX_MEM (
  input  [11:0] in_1,
  input  [11:0] in_2,
  input  [2:0] in_3,
  input  [1:0] in_4,
  input  in_5,
  input  in_6,
  output [11:0] out_7,
  output [11:0] out_8,
  output [2:0] out_9,
  output [1:0] out_10
);

  Register #(.width(12)) register_1 (.D(in_1), .en(in_5), .Q(out_7), .clk(in_6));  // open: clr
  Register #(.width(12)) register_2 (.D(in_2), .en(in_5), .Q(out_8), .clk(in_6));  // open: clr
  Register #(.width(3)) register_3 (.D(in_3), .en(in_5), .Q(out_9), .clk(in_6));  // open: clr
  Register #(.width(2)) register_4 (.D(in_4), .en(in_5), .Q(out_10), .clk(in_6));  // open: clr
endmodule

module MEM_WB (
  input  [11:0] in_1,
  input  in_2,
  input  [1:0] in_3,
  input  in_4,
  input  in_5,
  output [11:0] out_6,
  output out_7,
  output [1:0] out_8
);

  Register #(.width(12)) register_1 (.D(in_1), .en(in_4), .Q(out_6), .clk(in_5));  // open: clr
  Register #(.width(1)) register_2 (.D(in_2), .en(in_4), .Q(out_7), .clk(in_5));  // open: clr
  Register #(.width(2)) register_3 (.D(in_3), .en(in_4), .Q(out_8), .clk(in_5));  // open: clr
endmodule

module RegFile (
  input  [1:0] m1_sel,
  input  [11:0] in_2,
  input  [1:0] dec_sel,
  input  [1:0] m2_sel,
  input  write_enable,
  input  clock,
  output [11:0] out_7,
  output [11:0] out_8,
  output [11:0] out_9,
  output [11:0] out_10,
  output [11:0] out_11,
  output [11:0] out_12
);

  wire decoder_1_out0, decoder_1_out1, decoder_1_out2, decoder_1_out3;

  Decoder #(.select(2), .disabled(0)) decoder_1 (
    .out0(decoder_1_out0), .out1(decoder_1_out1), .out2(decoder_1_out2), .out3(decoder_1_out3),
    .sel(dec_sel), .en(write_enable));
  Register #(.width(12)) register_1 (.D(in_2), .en(decoder_1_out0), .Q(out_7), .clk(clock));  // open: clr
  Register #(.width(12)) register_2 (.D(in_2), .en(decoder_1_out1), .Q(out_8), .clk(clock));  // open: clr
  Register #(.width(12)) register_3 (.D(in_2), .en(decoder_1_out2), .Q(out_9), .clk(clock));  // open: clr
  Register #(.width(12)) register_4 (.D(in_2), .en(decoder_1_out3), .Q(out_10), .clk(clock));  // open: clr
  Multiplexer #(.select(2), .width(12), .disabled(0)) multiplexer_1 (
    .in0(out_7), .in1(out_8), .in2(out_9), .in3(out_10), .out(out_11), .sel(m1_sel));  // open: en
  Multiplexer #(.select(2), .width(12), .disabled(0)) multiplexer_2 (
    .in0(out_7), .in1(out_8), .in2(out_9), .in3(out_10), .out(out_12), .sel(m2_sel));  // open: en

  // Notes on the sheet:
  //   write data
  //   reg1 val
  //   reg2 val
  //   t0
  //   t1
  //   t2
  //   t3
  //   reg3 val
  //   reg4 val
  //   read data 1
  //   read data 2
endmodule

module Forwarding (
  input  [1:0] readreg1,
  input  [1:0] readreg2,
  input  [1:0] writereg1,
  input  [1:0] writereg2,
  output [1:0] r1,
  output [1:0] r2
);

  wire comparator_3_eq, comparator_4_eq;

  Comparator #(.width(2), .mode("unsigned")) comparator_1 (.a(readreg1), .b(writereg1), .eq(r1[0]));  // open: gt, lt
  Comparator #(.width(2), .mode("unsigned")) comparator_2 (.a(readreg2), .b(writereg1), .eq(r2[0]));  // open: gt, lt
  Comparator #(.width(2), .mode("unsigned")) comparator_3 (
    .a(readreg1), .b(writereg2), .eq(comparator_3_eq));  // open: gt, lt
  Comparator #(.width(2), .mode("unsigned")) comparator_4 (
    .a(readreg2), .b(writereg2), .eq(comparator_4_eq));  // open: gt, lt
  and and_1 (r1[1], ~r1[0], comparator_3_eq);  // AND_Gate
  and and_2 (r2[1], ~r2[0], comparator_4_eq);  // AND_Gate
endmodule
