// Logisim project sevenSegment.circ as structural Verilog: 1 circuit, main circuit main
module main (
  input  a,
  input  b,
  input  c
);

  wire _1_out, _2_out, _3_out, _4_out, _5_out, _6_out, _7_out, and_1_out, and_2_out, and_3_out, and_4_out,
       and_5_out, and_6_out, and_7_out, and_8_out, and_9_out, and_10_out, and_11_out, and_12_out, and_13_out,
       and_14_out, and_15_out, and_16_out, not_1_out, not_2_out, not_3_out;

  not not_1 (not_1_out, a);
  not not_2 (not_2_out, b);
  not not_3 (not_3_out, c);
  and and_1 (and_1_out, a, not_2_out);
  and and_2 (and_2_out, not_1_out, b);
  and and_3 (and_3_out, b, not_3_out);
  and and_4 (and_4_out, not_2_out, not_3_out);
  and and_5 (and_5_out, a, not_2_out);
  and and_6 (and_6_out, a, not_3_out);
  and and_7 (and_7_out, a, c);
  and and_8 (and_8_out, not_1_out, not_3_out);
  and and_9 (and_9_out, not_2_out, not_3_out);
  and and_10 (and_10_out, b, c);
  and and_11 (and_11_out, not_1_out, not_3_out);
  and and_12 (and_12_out, b, not_3_out);
  and and_13 (and_13_out, not_1_out, not_3_out);
  and and_14 (and_14_out, not_1_out, b);
  and and_15 (and_15_out, b, not_3_out);
  and and_16 (and_16_out, a, not_2_out, c);
  or _1 (_1_out, and_1_out, and_2_out, and_3_out);
  or _2 (_2_out, and_4_out, and_5_out, and_6_out);
  or _3 (_3_out, b, and_7_out, and_8_out);
  or _4 (_4_out, not_1_out, and_9_out, and_10_out);
  or _5 (_5_out, and_11_out, and_12_out);
  or _6 (_6_out, and_13_out, and_14_out, and_15_out, and_16_out);
  or _7 (_7_out, a, not_2_out, c);
  _7_Segment_Display u_7_segment_display_1 (
    .g(_1_out), .f(_2_out), .a(_3_out), .b(_4_out), .e(_5_out), .d(_6_out), .c(_7_out));  // open: dp

  // Notes on the sheet:
  //   Max Goldberg and Peter Richieri HW 8
endmodule
