// Logisim project HW9.circ as structural Verilog: 1 circuit, main circuit main
module main (
  input  in_1
);

  wire add_out, beq_2_out, beq_out, bne_2_out, bne_out, clock_1_out, decoder_1_out0, decoder_1_out1,
       decoder_1_out2, decoder_1_out3, imm_0_out, imm_out, lw_out, not_1_out, not_2_out, not_3_out,
       not_4_out, not_5_out, or_1_out, or_2_out, or_3_out, sub_out, subi_out, sw_out, undriven, writereg_out;
  wire [1:0] multiplexer_2_out;
  wire [4:0] ram_1_data;
  wire [11:0] adder_1_out, adder_2_out, adder_3_out, multiplexer_1_out, multiplexer_3_out, multiplexer_4_out,
       multiplexer_5_out, multiplexer_6_out, multiplexer_7_out, not_6_out, ram_2_data, register_1_q,
       register_2_q, register_3_q, register_4_q, register_5_q;
  wire [11:5] ram_1_data_2;

  Register #(.width(12)) register_1 (.D(multiplexer_1_out), .Q(register_1_q), .clk(clock_1_out));  // open: en, clr
  Adder #(.width(12)) adder_1 (.a(12'h1), .b(register_1_q), .out(adder_1_out));  // open: cin, cout
  Multiplexer #(.width(12)) multiplexer_1 (
    .in0(adder_1_out), .in1({{7{1'b0}}, ram_1_data}), .out(multiplexer_1_out), .sel(or_1_out), .en(undriven));
  and beq (beq_out, ~imm_0_out, beq_2_out);  // AND_Gate
  or or_1 (or_1_out, beq_out, bne_out);
  and bne (bne_out, imm_0_out, bne_2_out);
  RAM #(.addrWidth(12), .dataWidth(12), .bus("separate")) ram_1 (
    .addr(register_1_q), .data({ram_1_data_2, ram_1_data}));  // open: din, str, sel, clk, ld, clr
  or imm_0 (imm_0_out, adder_3_out[0], adder_3_out[1], adder_3_out[2], adder_3_out[3], adder_3_out[4], adder_3_out[5], adder_3_out[6], adder_3_out[7], adder_3_out[8], adder_3_out[9], adder_3_out[10], adder_3_out[11]);
  // Probe on {{7{1'b0}}, ram_1_data}
  Decoder #(.select(2), .disabled(0)) decoder_1 (
    .out0(decoder_1_out0), .out1(decoder_1_out1), .out2(decoder_1_out2), .out3(decoder_1_out3),
    .sel(multiplexer_2_out), .en(writereg_out));
  Multiplexer #(.width(2)) multiplexer_2 (
    .in0(ram_1_data[4:3]), .in1(ram_1_data_2[6:5]), .out(multiplexer_2_out), .sel(not_4_out));  // open: en
  not not_1 (not_1_out, ram_1_data_2[11]);
  not not_2 (not_2_out, ram_1_data_2[10]);
  Clock clock_1 (.out(clock_1_out));
  not not_3 (not_3_out, ram_1_data_2[9]);
  Register #(.width(12)) register_2 (
    .D(multiplexer_7_out), .en(decoder_1_out0), .Q(register_2_q), .clk(clock_1_out));  // open: clr
  Register #(.width(12)) register_3 (
    .D(multiplexer_7_out), .en(decoder_1_out1), .Q(register_3_q), .clk(clock_1_out));  // open: clr
  Register #(.width(12)) register_4 (
    .D(multiplexer_7_out), .en(decoder_1_out2), .Q(register_4_q), .clk(clock_1_out));  // open: clr
  Register #(.width(12)) register_5 (
    .D(multiplexer_7_out), .en(decoder_1_out3), .Q(register_5_q), .clk(clock_1_out));  // open: clr
  and add (add_out, not_3_out, not_2_out, not_1_out);
  and sub (sub_out, ram_1_data_2[9], not_2_out, not_1_out);
  // AND_Gate addi has open pins: in0=not_1_out, in1=ram_1_data_2[10], in2=not_3_out, out=open
  and subi (subi_out, not_1_out, ram_1_data_2[10], ram_1_data_2[9]);
  and beq_2 (beq_2_out, ram_1_data_2[11], not_2_out, not_3_out);
  and bne_2 (bne_2_out, ram_1_data_2[11], not_2_out, ram_1_data_2[9]);
  and sw (sw_out, ram_1_data_2[11], ram_1_data_2[10], not_3_out);
  and lw (lw_out, ram_1_data_2[9], ram_1_data_2[10], ram_1_data_2[11]);
  Multiplexer #(.select(2), .width(12), .disabled(0), .enable("false")) multiplexer_3 (
    .in0(register_2_q), .in1(register_3_q), .in2(register_4_q), .in3(register_5_q), .out(multiplexer_3_out),
    .sel(ram_1_data_2[8:7]));
  Multiplexer #(.select(2), .width(12), .disabled(0), .enable("false")) multiplexer_4 (
    .in0(register_2_q), .in1(register_3_q), .in2(register_4_q), .in3(register_5_q), .out(multiplexer_4_out),
    .sel(ram_1_data_2[6:5]));
  not not_4 (not_4_out, or_2_out);
  or or_2 (or_2_out, add_out, sub_out);
  // Probe on multiplexer_3_out
  Multiplexer #(.width(12)) multiplexer_5 (
    .in0(multiplexer_4_out), .in1({{7{1'b0}}, ram_1_data}), .out(multiplexer_5_out), .sel(not_5_out));  // open: en
  // Probe on multiplexer_4_out
  not not_5 (not_5_out, imm_out);
  or imm (imm_out, or_2_out, beq_2_out, bne_2_out);
  assign not_6_out = ~multiplexer_5_out;  // NOT_Gate not_6, 12 bits wide
  nor writereg (writereg_out, beq_2_out, sw_out, bne_2_out);
  Adder #(.width(12)) adder_2 (.a(not_6_out), .b({12{1'b0}}), .out(adder_2_out), .cin(in_1));  // open: cout
  or or_3 (or_3_out, sub_out, subi_out, beq_2_out, bne_2_out);
  // Probe on multiplexer_6_out
  Multiplexer #(.width(12)) multiplexer_6 (
    .in0(multiplexer_5_out), .in1(adder_2_out), .out(multiplexer_6_out), .sel(or_3_out));  // open: en
  Multiplexer #(.width(12)) multiplexer_7 (
    .in0(adder_3_out), .in1(ram_2_data), .out(multiplexer_7_out), .sel(lw_out));  // open: en
  Adder #(.width(12)) adder_3 (.a(multiplexer_3_out), .b(multiplexer_6_out), .out(adder_3_out));  // open: cin, cout
  RAM #(.addrWidth(12), .dataWidth(12), .bus("separate")) ram_2 (
    .addr(adder_3_out), .din(multiplexer_4_out), .data(ram_2_data), .str(sw_out), .sel(1'b1),
    .clk(clock_1_out), .ld(lw_out));  // open: clr

  // Notes on the sheet:
  //   PC
  //   Instruction Mem
  //   op code
  //   t0
  //   t1
  //   t2
  //   t3
  //   Main Memory
endmodule
