// Logisim project HW9start.circ as structural Verilog: 1 circuit, main circuit main
module main (
);

  wire clock_1_out, decoder_1_out0, decoder_1_out1, decoder_1_out2, decoder_1_out3;
  wire [2:0] ram_1_data_2;
  wire [8:0] ram_1_data;
  wire [11:0] adder_1_out, adder_2_out, multiplexer_1_out, multiplexer_2_out, register_1_q, register_2_q,
       register_3_q, register_4_q, register_5_q;

  Adder #(.width(12)) adder_1 (.a(12'h1), .b(register_1_q), .out(adder_1_out));  // open: cin, cout
  Register #(.width(12)) register_1 (.D(adder_1_out), .Q(register_1_q), .clk(clock_1_out));  // open: en, clr
  RAM #(.addrWidth(12), .dataWidth(12), .bus("separate")) ram_1 (
    .addr(register_1_q), .data({ram_1_data_2, ram_1_data}));  // open: din, str, sel, clk, ld, clr
  Decoder #(.select(2), .disabled(0)) decoder_1 (
    .out0(decoder_1_out0), .out1(decoder_1_out1), .out2(decoder_1_out2), .out3(decoder_1_out3),
    .sel(ram_1_data[4:3]));  // open: en
  Clock clock_1 (.out(clock_1_out));
  Register #(.width(12)) register_2 (
    .D(adder_2_out), .en(decoder_1_out0), .Q(register_2_q), .clk(clock_1_out));  // open: clr
  Register #(.width(12)) register_3 (
    .D(adder_2_out), .en(decoder_1_out1), .Q(register_3_q), .clk(clock_1_out));  // open: clr
  Register #(.width(12)) register_4 (
    .D(adder_2_out), .en(decoder_1_out2), .Q(register_4_q), .clk(clock_1_out));  // open: clr
  Register #(.width(12)) register_5 (
    .D(adder_2_out), .en(decoder_1_out3), .Q(register_5_q), .clk(clock_1_out));  // open: clr
  Multiplexer #(.select(2), .width(12), .disabled(0), .enable("false")) multiplexer_1 (
    .in0(register_2_q), .in1(register_3_q), .in2(register_4_q), .in3(register_5_q), .out(multiplexer_1_out),
    .sel(ram_1_data[8:7]));
  Multiplexer #(.select(2), .width(12), .disabled(0), .enable("false")) multiplexer_2 (
    .in0(register_2_q), .in1(register_3_q), .in2(register_4_q), .in3(register_5_q), .out(multiplexer_2_out),
    .sel(ram_1_data[6:5]));
  // Probe on multiplexer_1_out
  Adder #(.width(12)) adder_2 (.a(multiplexer_1_out), .b(multiplexer_2_out), .out(adder_2_out));  // open: cin, cout
  // Probe on multiplexer_2_out
  RAM #(.addrWidth(12), .dataWidth(12), .bus("separate")) ram_2 (.clk(clock_1_out));  // open: addr, din, data, str, sel, ld, clr

  // Notes on the sheet:
  //   PC
  //   Instruction Mem
  //   op code
  //   t0
  //   t1
  //   t2
  //   t3
  //   Main Memory
endmodule
